# Fritzing sketch LEDResistor (saved by Fritzing 0.9.3b)
breadboards: 1

parts:
  LED = LED - 5mm [color="Red (633nm)" package="5 mm [THT]"]
  R = Resistor [tolerance=±5% resistance=220 package=THT]
  Part1 = Arduino Uno (Rev3)

nets:
  N1: LED.cathode, R.Pin_0
  5V: LED.anode, Part1.5V
  GND: R.Pin_1, Part1.GND
