# Fritzing sketch LEDResistorButton (saved by Fritzing 0.9.3b)
breadboards: 1

parts:
  LED = LED - 5mm [color="Red (633nm)" package="5 mm [THT]"]
  Part1 = Arduino Uno (Rev3)
  R1 = Resistor [tolerance=±5% resistance=220 package=THT]
  S1 = Pushbutton [package="[THT]"]

nets:
  N1: LED.cathode, R1.Pin_1
  5V: LED.anode, Part1.5V
  N2: Part1.GND, S1.Pin_3, S1.Pin_4
  N3: R1.Pin_0, S1.Pin_1, S1.Pin_2
