# Fritzing sketch ArduinoLEDButton (saved by Fritzing 0.9.3b)
breadboards: 1

parts:
  LED = LED - 5mm [color="Red (633nm)" package="5 mm [THT]"]
  Arduino = Arduino Uno (Rev3)
  Switch = Pushbutton [package="[THT]"]
  R = Resistor [tolerance=±5% resistance=220 package=THT]

nets:
  N1: LED.cathode, Arduino.GND, Switch.Pin_1, Switch.Pin_2
  N2: LED.anode, R.Pin_0
  N3: Arduino.D2, Switch.Pin_3, Switch.Pin_4
  N4: Arduino.D6_PWM, R.Pin_1
