# Fritzing sketch OneBlinkingLED (saved by Fritzing 0.9.3b)
breadboards: 1

parts:
  LED = LED - 5mm [color="Red (633nm)" package="5 mm [THT]"]
  Arduino = Arduino Uno (Rev3)
  R = Resistor [tolerance=±5% resistance=220 package=THT]

nets:
  N1: LED.cathode, Arduino.GND
  N2: LED.anode, R.Pin_0
  N3: Arduino.D6_PWM, R.Pin_1
