# Fritzing sketch Dice (saved by Fritzing 0.9.3b)
breadboards: 1

parts:
  Arduino = Arduino Uno (Rev3)
  7_Segment2 = 7 Segment Display
  R1 = Resistor [tolerance=±5% resistance=220 package=THT]
  R2 = Resistor [tolerance=±5% resistance=220 package=THT]
  R3 = Resistor [tolerance=±5% resistance=220 package=THT]
  R4 = Resistor [tolerance=±5% resistance=220 package=THT]
  R5 = Resistor [tolerance=±5% resistance=220 package=THT]
  R6 = Resistor [tolerance=±5% resistance=220 package=THT]
  R7 = Resistor [tolerance=±5% resistance=220 package=THT]
  S1 = Pushbutton [package="[THT]"]

nets:
  N1: Arduino.D8, R5.Pin_1
  N2: Arduino.D9_PWM, S1.Pin_1, S1.Pin_2
  N3: Arduino.GND, 7_Segment2.common_cathode, S1.Pin_3, S1.Pin_4
  N4: Arduino.D2, R1.Pin_1
  N5: Arduino.D3_PWM, R2.Pin_1
  N6: Arduino.D4, R3.Pin_0
  N7: Arduino.D5_PWM, R4.Pin_0
  N8: Arduino.D6_PWM, R6.Pin_0
  N9: Arduino.D7, R7.Pin_0
  N10: 7_Segment2.Segment_E, R6.Pin_1
  N11: 7_Segment2.Segment_D, R7.Pin_1
  N12: 7_Segment2.Segment_C, R5.Pin_0
  N13: 7_Segment2.Segment_B, R1.Pin_0
  N14: 7_Segment2.Segment_A, R2.Pin_0
  N15: 7_Segment2.Segment_F, R4.Pin_1
  N16: 7_Segment2.Segment_G, R3.Pin_1
