# Fritzing sketch TwoBlinkingLEDs (saved by Fritzing 0.9.3b)
breadboards: 1

parts:
  LED = LED - 5mm [color="Red (633nm)" package="5 mm [THT]"]
  Arduino = Arduino Uno (Rev3)
  R = Resistor [tolerance=±5% resistance=220 package=THT]
  LED1 = LED - 5mm [color="Green (555nm)" package="5 mm [THT]"]
  R1 = Resistor [tolerance=±5% resistance=220 package=THT]

nets:
  N1: LED.cathode, Arduino.GND, LED1.cathode
  N2: LED.anode, R.Pin_0
  N3: Arduino.D6_PWM, R.Pin_1
  N4: Arduino.D7, R1.Pin_1
  N5: LED1.anode, R1.Pin_0
