# Fritzing sketch ArduinoLEDPotentiometer (saved by Fritzing 0.9.3b)
breadboards: 1

parts:
  LED = LED - 5mm [color="Red (633nm)" package="5 mm [THT]"]
  Arduino = Arduino Uno (Rev3)
  R = Resistor [tolerance=±5% resistance=220 package=THT]
  R1 = Rotary Potentiometer (Large) [maximum_resistance=100kΩ package=THT]

nets:
  N1: LED.cathode, Arduino.GND, R1.leg1
  N2: LED.anode, R.Pin_0
  N3: Arduino.A0, R1.wiper
  N4: Arduino.D6_PWM, R.Pin_1
  N5: Arduino.5V, R1.leg2
