# Fritzing sketch IRReceiverLED (saved by Fritzing 0.9.3b)
breadboards: 1

parts:
  LED = LED - 5mm [color="Red (633nm)" package="5 mm [THT]"]
  Arduino = Arduino Uno (Rev3)
  R = Resistor [tolerance=±5% resistance=220 package=THT]
  Part2 = IR_reviever

nets:
  N1: LED.cathode, Part2.connector10
  N2: LED.anode, R.Pin_0
  N3: Arduino.5V, R.Pin_1, Part2.connector9
  N4: Arduino.GND, Part2.connector8
