# Fritzing sketch IRReceiver (saved by Fritzing 0.9.3b)
breadboards: 1

parts:
  Arduino = Arduino Uno (Rev3)
  Part2 = Infra red receiver

nets:
  N1: Arduino.D11_PWM/MOSI, Part2.Data
  5V: Arduino.5V, Part2.VCC
  GND: Arduino.GND, Part2.GND
