# Fritzing sketch IRSender (saved by Fritzing 0.9.3b)
breadboards: 1

parts:
  Arduino = Arduino Uno (Rev3)
  R1 = Resistor [tolerance=±5% resistance=220 package=THT]
  LED2 = smd LED [color="Infrared (940nm)" package="0805 [SMD]"]

nets:
  N1: Arduino.D3_PWM, LED2.anode
  N2: Arduino.GND, R1.Pin_0
  N3: R1.Pin_1, LED2.cathode
