# Fritzing sketch IRReceiverLED (saved by Fritzing 0.9.3b)
breadboards: 1

parts:
  Arduino = Arduino Uno (Rev3)
  Part2 = Infra red receiver
  R1 = Resistor [tolerance=±5% resistance=220 package=THT]
  LED1 = LED - 5mm [color="Red (633nm)" package="5 mm [THT]"]

nets:
  N1: Arduino.D11_PWM/MOSI, Part2.Data
  N2: Arduino.D2, LED1.anode
  5V: Arduino.5V, Part2.VCC
  GND: Arduino.GND, Part2.GND, R1.Pin_0
  N3: R1.Pin_1, LED1.cathode
