# Fritzing sketch IRSenderButton (saved by Fritzing 0.9.3b)
breadboards: 1

parts:
  Arduino = Arduino Uno (Rev3)
  R1 = Resistor [tolerance=±5% resistance=220 package=THT]
  LED2 = smd LED [color="Infrared (940nm)" package="0805 [SMD]"]
  Switch1 = Pushbutton [package="[THT]"]

nets:
  N1: Arduino.D3_PWM, LED2.anode
  N2: Arduino.D7, Switch1.Pin_3, Switch1.Pin_4
  N3: Arduino.GND, R1.Pin_0, Switch1.Pin_1, Switch1.Pin_2
  N4: R1.Pin_1, LED2.cathode
