# Fritzing sketch ESP8266Programmer (saved by Fritzing 0.9.3b)
breadboards: 1

parts:
  U2 = ESP8266 WiFi Module [part_number=ESP8266]
  Part3 = FTDI Basic Programmer
  S1 = Pushbutton [package="[SMD]"]
  S2 = Pushbutton [package="[THT]"]

nets:
  N1: U2.RXD, Part3.TXO
  N2: U2.VCC, U2.CH_PD, Part3.POWER
  N3: U2.GPIO_0, S2.Pin_1, S2.Pin_2
  N4: U2.RST, S1.Pin_1, S1.Pin_2
  GND: U2.GND, Part3.GND, S1.Pin_3, S1.Pin_4, S2.Pin_3, S2.Pin_4
  N5: U2.TXD, Part3.RXI

notes:
  Reset
  Button
  Flash
  Button

custom parts:
  ESP8266 WiFi Module: Generic WiFi Module based on the ESP8266 with onboard PCB antenna and UART communications
